// Logisim project or-no-ttriger.circ as structural Verilog: 1 circuit, main circuit main
module main (
);

  wire clock_1_out, nand_1_out, not_1_out, not_2_out, not_3_out, not_4_out;
  wire [2:0] T1_q;

  not not_1 (not_1_out, T1_q[0]);
  not not_2 (not_2_out, T1_q[1]);
  nand nand_1 (nand_1_out, not_1_out, not_2_out);
  not not_3 (not_3_out, nand_1_out);
  Clock clock_1 (.out(clock_1_out));
  not not_4 (not_4_out, T1_q[0]);
  T_Flip_Flop T3 (.clk(clock_1_out), .T(not_3_out), .Q(T1_q[2]));  // open: Qn, preset, reset, en
  T_Flip_Flop T2 (.clk(clock_1_out), .T(not_4_out), .Q(T1_q[1]));  // open: Qn, preset, reset, en
  T_Flip_Flop T1 (.clk(clock_1_out), .T(1'b1), .Q(T1_q[0]));  // open: Qn, preset, reset, en
  // Probe on T1_q
endmodule
